# Fritzing sketch controller (saved by Fritzing 0.7.10b)
breadboards: 1

parts:
  Teensy1 = Teensy 2.0
  VCC1 = 4 x AAA Battery Mount
  IC1 = L293D [package=THT]
  M1 = DC Motor
  M2 = DC Motor

nets:
  N1: Teensy1.GND, VCC1.-, IC1.0V
  N2: Teensy1.F7, IC1.In_2
  N3: Teensy1.F6, IC1.In_1
  N4: Teensy1.F5, IC1.Enable_1
  N5: Teensy1.F4, IC1.In_3
  N6: Teensy1.F1, IC1.In_4
  N7: Teensy1.F0, IC1.Enable_2
  N8: Teensy1.VCC, IC1.+V
  N9: VCC1.+, IC1.+Vmotor
  N10: IC1.Out_1_(_Controlled_by_Enable_1_), M1.pin_2
  N11: IC1.Out_2_(_Controlled_by_Enable_1_), M1.pin_1
  N12: IC1.Out_3_(_Controlled_by_Enable_2_), M2.pin_2
  N13: IC1.Out_4_(_Controlled_by_Enable_2_), M2.pin_1
